# Fritzing sketch CdsLed (saved by Fritzing 0.8.7b)
circuit board: 4.47626cm x 3.61229cm
perfboards: 1

parts:
  PIC12F675 = IC, DIP package, 8 pins
  VCC1 = Battery
  LED1 = LED - 5mm [color="White (6500K)" package="5 mm [THT]"]
  R1 = Resistor [tolerance=±5% resistance=68 package=THT]
  R2 = Resistor [tolerance=±5% resistance=10k package=THT]
  R3 = PHOTOCELL [package=photocell-kit]

nets:
  N1: PIC12F675.pin1, VCC1.+, R2.Pin_0
  N2: PIC12F675.pin4, R2.Pin_1, R3.P$2
  N3: PIC12F675.pin5, LED1.anode
  N4: PIC12F675.pin8, R1.Pin_0
  N5: VCC1.-, R3.P$1
  N6: LED1.cathode, R1.Pin_1
