# Fritzing sketch SpeakerSensor (saved by Fritzing 0.8.7b)
perfboards: 1

parts:
  パーツ1 = Arduino Uno (Rev3)
  Q1 = NPN-Transistor [package="TO92 [THT]"]
  Q2 = NPN-Transistor [package="TO92 [THT]"]
  R1 = Resistor [tolerance=±5% resistance=4.7 package=THT]
  R2 = Trimmer Potentiometer [maximum_resistance=10kΩ package=THT]
  R3 = Resistor [tolerance=±5% resistance=100k package=THT]
  C1 = Ceramic Capacitor [capacitance=100nF package="100 mil [THT, multilayer]"]
  R4 = Resistor [tolerance=±5% resistance=47 package=THT]
  J1 = Piezo Speaker

nets:
  N1: パーツ1.A5/SCL, Q1.C, Q2.B, Q2.C, R1.Pin_1, R2.leg1, R3.Pin_1, C1.0
  N2: パーツ1.5V, R1.Pin_0, R3.Pin_0
  N3: パーツ1.GND, Q1.E, R2.wiper, R4.Pin_1, J1.pin1
  N4: Q1.B, Q2.E
  N5: C1.1, R4.Pin_0, J1.pin2
