# Fritzing sketch arduino (saved by Fritzing 0.8.7b)
perfboards: 1

parts:
  C1 = Ceramic Capacitor [capacitance=100nF package="100 mil [THT, multilayer]"]
  U1 = atmega328 [package=dip]
  S1 = Pushbutton [package="[THT]"]
  R1 = Resistor [tolerance=±5% resistance=10k package=THT]
  XTAL1 = Crystal [frequency="16 Mhz" package=THT]
  C2 = Ceramic Capacitor [capacitance=10pF package="100 mil [THT, multilayer]"]
  C3 = Ceramic Capacitor [capacitance=10pF package="100 mil [THT, multilayer]"]
  IC1 = IC, DIP package, 20 pins [chip_label=PIC18F14K50]
  R2 = Resistor [tolerance=±5% resistance=1k package=THT]
  R3 = Resistor [tolerance=±5% resistance=1k package=THT]
  XTAL2 = Crystal [frequency="16 Mhz" package=THT]
  C5 = Ceramic Capacitor [capacitance=10pF package="100 mil [THT, multilayer]"]
  C6 = Ceramic Capacitor [capacitance=10pF package="100 mil [THT, multilayer]"]
  C7 = Ceramic Capacitor [capacitance=100nF package="100 mil [THT, multilayer]"]
  C8 = Ceramic Capacitor [capacitance=10µF package="100 mil [THT, multilayer]"]  # not connected
  C9 = Ceramic Capacitor [capacitance=0.1nF package="100 mil [THT, multilayer]"]  # not connected
  C4 = Ceramic Capacitor [capacitance=100nF package="100 mil [THT, multilayer]"]

nets:
  N1: C1.1, U1.GND#7, S1.Pin_1, S1.Pin_2, IC1.pin17, C7.0
  N2: U1.RESET, S1.Pin_3, S1.Pin_4, R1.Pin_1, C4.1
  N3: U1.D0_(RX), R3.Pin_0
  N4: U1.D1_(TX), R2.Pin_0
  N5: U1.XLAT1, XTAL1.pin_0, C2.1
  N6: U1.XLAT2, XTAL1.pin_1, C3.1
  N7: C2.0, C3.0
  N8: IC1.pin2, XTAL2.pin_1, C5.1
  N9: IC1.pin3, XTAL2.pin_0, C6.1
  N10: IC1.pin10, R3.Pin_1
  N11: IC1.pin12, R2.Pin_1
  N12: C5.0, C6.0, C7.1
